// Digital circuit Template.dig as structural Verilog
module Template (
  input  X0,
  input  X1,
  input  S1,
  input  X2,
  input  X3,
  input  S0,
  output Z
);

  wire and_1_out, and_2_out, and_3_out, and_4_out, s0n, s1n;

  not not_1 (s1n, S1);
  not not_2 (s0n, S0);
  and and_1 (and_1_out, s0n, s1n, X0);
  and and_2 (and_2_out, S0, s1n, X1);
  and and_3 (and_3_out, s0n, S1, X2);
  and and_4 (and_4_out, S0, S1, X3);
  or or_1 (Z, and_1_out, and_2_out, and_3_out, and_4_out);
endmodule
