// Digital circuit Template.dig as structural Verilog
module Template (
  input  [2:0] In,
  input  clk,
  input  [2:0] In_2,
  output [7:0] Z
);

  Terminal Digital (.D(Z), .C(clk), .en(1'b1));
endmodule
